// Logisim project BreadboardComputer.circ as structural Verilog
module ALU (
  input  [15:0] input_a,
  input  [15:0] input_b,
  input  in_3,
  input  [1:0] in_4,
  input  in_5,
  output [15:0] out_6
);

  wire adder_1_cout, demultiplexer_1_out1, demultiplexer_1_out2, demultiplexer_1_out3, not_1_out;
  wire [15:0] adder_1_out, controlled_buffer_1_out, nand_1_out, xor_1_out;

  assign xor_1_out = input_a ^ input_b;  // XOR_Gate xor_1, 16 bits wide
  assign controlled_buffer_1_out = demultiplexer_1_out3 ? xor_1_out : 16'bz;  // Controlled_Buffer controlled_buffer_1
  assign out_6 = not_1_out ? controlled_buffer_1_out : 16'bz;  // Controlled_Buffer controlled_buffer_2
  assign nand_1_out = ~(input_b & input_a);  // NAND_Gate nand_1, 16 bits wide
  assign controlled_buffer_1_out = demultiplexer_1_out2 ? adder_1_out : 16'bz;  // Controlled_Buffer controlled_buffer_3
  assign controlled_buffer_1_out = demultiplexer_1_out1 ? nand_1_out : 16'bz;  // Controlled_Buffer controlled_buffer_4
  Adder #(.width(16)) adder_1 (.a(input_b), .b(input_a), .out(adder_1_out), .cout(adder_1_cout));  // open: cin
  assign out_6 = in_5 ? {1'b0, controlled_buffer_1_out[15:1]} : 16'bz;  // Controlled_Buffer controlled_buffer_5
  not not_1 (not_1_out, in_5);
  Demultiplexer #(.select(2)) demultiplexer_1 (
    .out1(demultiplexer_1_out1), .out2(demultiplexer_1_out2), .out3(demultiplexer_1_out3), .in(in_3),
    .sel(in_4));  // open: out0
endmodule
